# Fritzing sketch 03 LED (saved by Fritzing 1.0.5)
breadboards: 1

parts:
  Ard1 = Arduino Uno (Rev3) - ICSP
  R1 = Resistor [tolerance=±5% power=0.25W resistance=330 package=THT]
  LED1 = LED - 5mm [color="Red (633nm)" current=0.030A package="5 mm [THT]"]

nets:
  N1: Ard1.D8, R1.Pin_0
  N2: Ard1.GND, LED1.cathode
  N3: R1.Pin_1, LED1.anode
