# Fritzing sketch 04 RGB LED (saved by Fritzing 1.0.5)
breadboards: 1

parts:
  RGB_LED1 = RGB LED (com. cathode, rbg) [color="Red (633nm)" current=0.030A package="5 mm [THT]"]
  R1 = Resistor [tolerance=±5% power=0.25W resistance=330 package=THT]
  R2 = Resistor [tolerance=±5% power=0.25W resistance=330 package=THT]
  R3 = Resistor [tolerance=±5% power=0.25W resistance=330 package=THT]
  UNO1 = Arduino Uno (Rev3) - ICSP

nets:
  N1: RGB_LED1.red_anode, R1.Pin_1
  N2: RGB_LED1.common_cathode, UNO1.GND
  N3: RGB_LED1.blue_anode, R2.Pin_1
  N4: RGB_LED1.green_anode, R3.Pin_1
  N5: R1.Pin_0, UNO1.D3_PWM
  N6: R2.Pin_0, UNO1.D5_PWM
  N7: R3.Pin_0, UNO1.D6_PWM
