# Fritzing sketch 05 Push Button (saved by Fritzing 1.0.5)
breadboards: 1

parts:
  Part1 = Arduino Uno (Rev3) - ICSP
  R1 = Resistor [tolerance=±5% power=0.25W resistance=330 package=THT]
  R2 = Resistor [tolerance=±5% power=0.25W resistance=1k package=THT]
  LED1 = LED - 5mm [color="Red (633nm)" current=0.030A package="5 mm [THT]"]
  S_A_-_Pull_Down = Momentary Switch [package=ksa_sealed_tac_switch]
  R3 = Resistor [tolerance=±5% power=0.25W resistance=1k package=THT]
  S_B_-_Pull_Up = Momentary Switch [package=ksa_sealed_tac_switch]

nets:
  N1: Part1.D13/SCK, R1.Pin_0
  N2: Part1.GND, LED1.cathode, R3.Pin_1, S_B_-_Pull_Up.3, S_B_-_Pull_Up.4
  N3: Part1.D2, S_A_-_Pull_Down.1, S_A_-_Pull_Down.2, R3.Pin_0
  N4: Part1.D3_PWM, R2.Pin_1, S_B_-_Pull_Up.1, S_B_-_Pull_Up.2
  N5: Part1.5V, R2.Pin_0, S_A_-_Pull_Down.3, S_A_-_Pull_Down.4
  N6: R1.Pin_1, LED1.anode
