# Fritzing sketch 09 Servo (saved by Fritzing 1.0.5)
breadboards: 1

parts:
  Part1 = Arduino Uno (Rev3) - ICSP
  J1 = Basic Servo

nets:
  5V: Part1.5V, J1.vcc
  N1: Part1.D9_PWM, J1.pulse
  GND: Part1.GND, J1.gnd
