# Fritzing sketch 11 Membrane Switch (saved by Fritzing 1.0.5)
breadboards: 1

parts:
  Part1 = Arduino Uno (Rev3) - ICSP
  KEYPAD1 = Membrane Matrix Keypad

nets:
  N1: Part1.D8, KEYPAD1.2
  N2: Part1.D9_PWM, KEYPAD1.1
  N3: Part1.D3_PWM, KEYPAD1.7
  N4: Part1.D4, KEYPAD1.6
  N5: Part1.D5_PWM, KEYPAD1.5
  N6: Part1.D6_PWM, KEYPAD1.4
  N7: Part1.D7, KEYPAD1.3

custom parts:
  Membrane Matrix Keypad: Membrane Matrix 3x4 Keypad
