# Fritzing sketch 12 DHT11 (saved by Fritzing 1.0.5)
breadboards: 1

parts:
  Part1 = Arduino Uno (Rev3) - ICSP
  DHT11 = DHT11 Humitidy and Temperature Sensor (3 pins)

nets:
  GND: Part1.GND, DHT11.Gnd
  N1: Part1.D2, DHT11.Signal
  N2: Part1.5V, DHT11.Plus

custom parts:
  DHT11 Humitidy and Temperature Sensor (3 pins): DHT11 Humidity and Temperature Sensor (3 pins).
