# Fritzing sketch 13 Joystick (saved by Fritzing 1.0.5)
breadboards: 1

parts:
  Part1 = Arduino Uno (Rev3) - ICSP
  Part3 = Adafruit Analog 2-Axis Joystick [part_number="Adafruit #512"]

nets:
  N1: Part1.A0, Part3.YOUT
  N2: Part1.A1, Part3.XOUT
  5V: Part1.5V, Part3.VCC
  GND: Part1.GND, Part3.GND
  N3: Part1.D2, Part3.SWITCH

custom parts:
  Adafruit Analog 2-Axis Joystick: This mini-kit makes it easy to mount a PSP/Xbox-like thumb joystick to your project. The thumbstick is an analog joystick - more accurate and sensitive than just 'directional' joysticks - with a 'press in to select' button. Since it's analog, you'll need two analog reading pins on your microcontroller to determine X and Y. Having an extra digital input will let you read the switch. The pack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
