# Fritzing sketch 17 HC-SR501 (saved by Fritzing 1.0.5)
breadboards: 1

parts:
  Part1 = Arduino Uno (Rev3) - ICSP
  PIR1 = PIR sensor
  LED1 = LED - 5mm [color="Red (633nm)" current=0.030A package="5 mm [THT]"]
  R1 = Resistor [tolerance=±5% power=0.25W resistance=330 package=THT]

nets:
  N1: Part1.D13/SCK, R1.Pin_0
  GND: Part1.GND, PIR1.GND, LED1.cathode
  N2: Part1.D2, PIR1.SIG
  5V: Part1.5V, PIR1.VDD
  N3: LED1.anode, R1.Pin_1
